// Logisim project 3bits_sum.circ as structural Verilog: 1 circuit, main circuit main
module main (
  input  a0,
  input  b0,
  input  a1,
  input  b1,
  input  a2,
  input  b2,
  output sumOut_0,
  output sumOut_1,
  output sumOut_2,
  output Carry
);

  wire and_1_out, and_2_out, and_3_out, and_4_out, and_5_out, or_1_out, xor_1_out, xor_2_out;

  xor xor_1 (xor_1_out, a1, b1);
  xor xor_2 (xor_2_out, a2, b2);
  xor xor_3 (sumOut_0, a0, b0);
  and and_1 (and_1_out, a0, b0);
  xor xor_4 (sumOut_1, and_1_out, xor_1_out);
  and and_2 (and_2_out, and_1_out, xor_1_out);
  and and_3 (and_3_out, a1, b1);
  and and_4 (and_4_out, or_1_out, xor_2_out);
  and and_5 (and_5_out, a2, b2);
  or or_1 (or_1_out, and_2_out, and_3_out);
  or or_2 (Carry, and_4_out, and_5_out);
  xor xor_5 (sumOut_2, or_1_out, xor_2_out);

  // Notes on the sheet:
  //   co
  //   ci
  //   co
  //   ci
endmodule
