// Logisim project b.circ as structural Verilog: 1 circuit, main circuit main
module main (
  input  e0,
  input  e1,
  input  e2,
  output b_out
);

  wire and_1_out, and_2_out, and_3_out, not_1_out, not_2_out, or_1_out;

  not not_1 (not_1_out, e0);
  not not_2 (not_2_out, e1);
  and and_1 (and_1_out, not_1_out, not_2_out);
  and and_2 (and_2_out, not_1_out, e2);
  and and_3 (and_3_out, not_2_out, e2);
  or or_1 (or_1_out, and_1_out, and_2_out);
  or or_2 (b_out, or_1_out, and_3_out);
endmodule
