// Logisim project conversor_7segmentos.circ as structural Verilog: 1 circuit, main circuit main
module main (
  input  in_1,
  input  in_2,
  input  in_3,
  output out_4,
  output out_5,
  output out_6,
  output out_7,
  output out_8,
  output out_9,
  output out_10
);

  g_main main_1 (.e0(in_1), .e1(in_2), .e2(in_3), .g_out(out_10));
  a_main main_2 (.e0(in_1), .e1(in_2), .e2(in_3), .a_out(out_4));
  b_main main_3 (.e0(in_1), .e1(in_2), .e2(in_3), .b_out(out_5));
  c_main main_4 (.e0(in_1), .e1(in_2), .e2(in_3), .c_out(out_6));
  d_main main_5 (.e0(in_1), .e1(in_2), .e2(in_3), .d_out(out_7));
  e_main main_6 (.e0(in_1), .e1(in_2), .e2(in_3), .e_out(out_8));
  f_main main_7 (.e0(in_1), .e1(in_2), .e2(in_3), .f_out(out_9));
endmodule
