// Logisim project f.circ as structural Verilog: 1 circuit, main circuit main
module main (
  input  e0,
  input  e1,
  input  e2,
  output f_out
);

  wire and_1_out, and_2_out, and_3_out, and_4_out, and_5_out, not_1_out, not_2_out, not_3_out, not_4_out,
       not_5_out, or_1_out, or_2_out;

  not not_1 (not_1_out, e0);
  not not_2 (not_2_out, e2);
  not not_3 (not_3_out, e0);
  and and_1 (and_1_out, not_1_out, not_2_out);
  and and_2 (and_2_out, not_3_out, e1);
  not not_4 (not_4_out, e2);
  or or_1 (or_1_out, and_1_out, and_2_out);
  and and_3 (and_3_out, e1, not_4_out);
  not not_5 (not_5_out, e1);
  and and_4 (and_4_out, e0, not_5_out);
  or or_2 (or_2_out, or_1_out, and_3_out);
  and and_5 (and_5_out, and_4_out, e2);
  or or_3 (f_out, or_2_out, and_5_out);
endmodule
