// Logisim project g.circ as structural Verilog: 1 circuit, main circuit main
module main (
  input  e0,
  input  e1,
  input  e2,
  output g_out
);

  wire not_1_out, or_1_out;

  not not_1 (not_1_out, e1);
  or or_1 (or_1_out, not_1_out, e2);
  or or_2 (g_out, e0, or_1_out);
endmodule
