// Logisim project projeto_final.circ as structural Verilog: 1 circuit, main circuit main
module main (
  input  a0,
  input  a1,
  input  a2,
  input  b0,
  input  b1,
  input  b2
);

  wire clock_1_out, main_1_sumout_0, main_1_sumout_1, main_1_sumout_2, main_2_o0, main_2_o1, main_2_o2,
       main_3_out_4, main_3_out_5, main_3_out_6, main_3_out_7, main_3_out_8, main_3_out_9, main_3_out_10;

  _3bits_sum_main main_1 (
    .a0(a0), .b0(b0), .a1(a1), .b1(b1), .a2(a2), .b2(b2), .sumOut_0(main_1_sumout_0),
    .sumOut_1(main_1_sumout_1), .sumOut_2(main_1_sumout_2));  // open: Carry
  Clock clock_1 (.out(clock_1_out));
  registrador_3bits_main main_2 (
    .i0(main_1_sumout_0), .i1(main_1_sumout_1), .i2(main_1_sumout_2), .o0(main_2_o0), .o1(main_2_o1),
    .o2(main_2_o2), .clk(clock_1_out));
  conversor_7segmentos_main main_3 (
    .in_1(main_2_o0), .in_2(main_2_o1), .in_3(main_2_o2), .out_4(main_3_out_4), .out_5(main_3_out_5),
    .out_6(main_3_out_6), .out_7(main_3_out_7), .out_8(main_3_out_8), .out_9(main_3_out_9),
    .out_10(main_3_out_10));
  _7_Segment_Display u_7_segment_display_1 (
    .g(main_3_out_4), .f(main_3_out_5), .a(main_3_out_6), .b(main_3_out_7), .e(main_3_out_8),
    .d(main_3_out_9), .c(main_3_out_10));  // open: dp
endmodule
