// Logisim project registrador-3bits.circ as structural Verilog: 1 circuit, main circuit main
module main (
  input  clk,
  input  i0,
  input  i1,
  input  i2,
  output o0,
  output o1,
  output o2
);

  D_Flip_Flop d_ff_1 (.clk(clk), .D(i0), .Q(o0));  // open: Qn, preset, en, reset
  D_Flip_Flop d_ff_2 (.clk(clk), .D(i1), .Q(o1));  // open: Qn, preset, en, reset
  D_Flip_Flop d_ff_3 (.clk(clk), .D(i2), .Q(o2));  // open: Qn, preset, en, reset
endmodule
